// Logisim project hw4.circ as structural Verilog: 5 circuits, main circuit main
// 128
module main (
  input  reset
);

  wire Available, ChangePC, clk, comparator_1_eq, comparator_2_lt, Load, M1, not_1_out, not_2_out, not_3_out,
       ReadKey, TTYOn, WE;
  wire [1:0] DestSelect, NewPCSelect, WSelect;
  wire [2:0] ALUOp, dest, rd, rs, rt, shamt;
  wire [3:0] opcode;
  wire [5:0] imm;
  wire [6:0] KeyInput;
  wire [11:0] j, PC;
  wire [15:0] adder_2_out, ALUResult, bit_extender_1_out, bit_extender_2_out, bit_extender_3_out, bltPC,
       bnePC, immPC, KeyData, multiplexer_3_out, multiplexer_5_out, NewPC, PC_1, RAMData, ReadData1,
       ReadData2, rom_1_data, WriteData;
  wire [15:12] jPC;

  Clock clock_1 (.out(clk));
  Keyboard keyboard_1 (.clk(clk), .re(ReadKey), .clr(reset), .avail(Available), .data(KeyInput));
  Register #(.width(16)) u_PC (.D(multiplexer_5_out), .Q({jPC, PC}), .clk(clk), .clr(reset));  // open: en
  Multiplexer #(.select(2), .width(16), .enable("false")) multiplexer_1 (
    .in0({jPC, j}), .in1(bnePC), .in2(bltPC), .in3(ReadData1), .out(NewPC), .sel(NewPCSelect));
  Adder #(.width(16)) adder_1 (.a({jPC, PC}), .b(16'h1), .out(PC_1));  // open: cin, cout
  Multiplexer #(.width(16), .enable("false")) multiplexer_2 (.in0(PC_1), .in1(immPC), .out(bnePC), .sel(not_1_out));
  Comparator #(.width(16)) comparator_1 (.a(ReadData1), .b(ReadData2), .eq(comparator_1_eq));  // open: gt, lt
  assign bit_extender_1_out = {{10{imm[5]}}, imm};  // Bit_Extender bit_extender_1
  assign bit_extender_2_out = {{9{1'b0}}, KeyInput};  // Bit_Extender bit_extender_2
  Adder #(.width(16)) adder_2 (.a(16'h1), .b({jPC, PC}), .out(adder_2_out));  // open: cin, cout
  not not_1 (not_1_out, comparator_1_eq);
  Multiplexer #(.width(16), .enable("false")) multiplexer_3 (
    .in0(ReadData2), .in1(bit_extender_1_out), .out(multiplexer_3_out), .sel(M1));
  Multiplexer #(.width(16), .enable("false")) multiplexer_4 (
    .in0(16'h80), .in1(bit_extender_2_out), .out(KeyData), .sel(Available));
  Multiplexer #(.width(16), .enable("false")) multiplexer_5 (
    .in0(adder_2_out), .in1(NewPC), .out(multiplexer_5_out), .sel(ChangePC));
  assign bit_extender_3_out = {{10{imm[5]}}, imm};  // Bit_Extender bit_extender_3
  // Probe on ALUOp
  Adder #(.width(16)) adder_3 (.a(PC_1), .b(bit_extender_3_out), .out(immPC));  // open: cin, cout
  Multiplexer #(.width(16), .enable("false")) multiplexer_6 (
    .in0(PC_1), .in1(immPC), .out(bltPC), .sel(comparator_2_lt));
  Comparator #(.width(16)) comparator_2 (.a(ReadData1), .b(ReadData2), .lt(comparator_2_lt));  // open: gt, eq
  ALU ALU (.OpType(ALUOp), .op1(ReadData1), .op2(multiplexer_3_out), .shamt(shamt), .OutputData(ALUResult));
  TTY #(.rows(13), .cols(80), .trigger("falling")) tty_1 (.data(ReadData1[6:0]), .clk(clk), .we(TTYOn), .clr(reset));
  // Probe on rom_1_data
  // Probe on ALUResult
  // Probe on ALUOp
  // Probe on DestSelect
  Control control_1 (
    .op(opcode), .ALUOp(ALUOp), .NewPCSelect(NewPCSelect), .Load(Load), .ChangePC(ChangePC), .TTYOn(TTYOn),
    .ReadKey(ReadKey), .WSelect(WSelect), .WE(WE), .M1(M1), .DestSelect(DestSelect));
  ROM #(.addrWidth(16), .dataWidth(16)) rom_1 (.addr({jPC, PC}), .data(rom_1_data));  // open: sel
  InstrDecoder InstrDecoder (
    .ROMInput(rom_1_data), .op(opcode), .rs(rs), .rt(rt), .rd(rd), .shamt(shamt), .j(j), .imm(imm));
  Multiplexer #(.select(2), .width(3), .enable("false")) multiplexer_7 (
    .in0(rd), .in1(rt), .in2(3'b111), .out(dest), .sel(DestSelect));  // open: in3
  RegisterFile RegisterFile (
    .ReadReg1(rs), .ReadReg2(rt), .WriteReg(dest), .WriteData(WriteData), .RegWriteEnable(WE), .clk(clk),
    .Reset(reset), .ReadData1(ReadData1), .ReadData2(ReadData2));
  not not_2 (not_2_out, clk);
  not not_3 (not_3_out, Load);
  Multiplexer #(.select(2), .width(16), .enable("false")) multiplexer_8 (
    .in0(ALUResult), .in1(RAMData), .in2(KeyData), .in3(PC_1), .out(WriteData), .sel(WSelect));
  // Probe on opcode
  RAM #(.addrWidth(16), .dataWidth(16), .bus("separate")) ram_1 (
    .addr(ALUResult), .din(ReadData2), .data(RAMData), .str(not_3_out), .clk(not_2_out));  // open: sel, ld, clr
  // Probe on dest
  // Probe on ReadData2
  // Probe on ReadData1

  // Other names for the same wires on the sheet: jPC[11:0] = j; PC[15:12] = jPC; res = reset

  // Notes on the sheet:
  //   contents of rom_1 (hex, n*v repeats v):
  //   2050 209f 3458 2070 2090 4458 c1ff 2fc1 c1ff
endmodule

module ALU (
  input  [2:0] OpType,
  input  [15:0] op1,
  input  [15:0] op2,
  input  [2:0] shamt,
  output [15:0] OutputData
);

  wire [3:0] bit_extender_1_out;
  wire [15:0] adder_1_out, not_1_out, shifter_1_out, shifter_2_out, subtractor_1_out, xor_1_out;

  assign bit_extender_1_out = {{1{1'b0}}, shamt};  // Bit_Extender bit_extender_1
  Adder #(.width(16)) adder_1 (.a(op1), .b(op2), .out(adder_1_out));  // open: cin, cout
  Subtractor #(.width(16)) subtractor_1 (.a(op1), .b(op2), .out(subtractor_1_out));  // open: bin, bout
  assign not_1_out = ~op1;  // NOT_Gate not_1, 16 bits wide
  assign xor_1_out = op1 ^ op2;  // XOR_Gate xor_1, 16 bits wide
  Shifter #(.width(16)) shifter_1 (.in(op1), .\dist (bit_extender_1_out), .out(shifter_1_out));
  Shifter #(.width(16), .shift("ar")) shifter_2 (.in(op1), .\dist (bit_extender_1_out), .out(shifter_2_out));
  Multiplexer #(.select(3), .width(16), .enable("false")) multiplexer_1 (
    .in0(adder_1_out), .in1(subtractor_1_out), .in2(not_1_out), .in3(xor_1_out), .in4(shifter_1_out),
    .in5(shifter_2_out), .out(OutputData), .sel(OpType));  // open: in6, in7

  // Other names for the same wires on the sheet: OT[2:0] = OpType
endmodule

module RegisterFile (
  input  [2:0] ReadReg1,
  input  [2:0] ReadReg2,
  input  [2:0] WriteReg,
  input  [15:0] WriteData,
  input  RegWriteEnable,
  input  clk,
  input  Reset,
  output [15:0] ReadData1,
  output [15:0] ReadData2
);

  wire and_1_out, and_2_out, and_3_out, and_4_out, and_5_out, and_6_out, and_7_out, and_8_out,
       decoder_1_out0, decoder_1_out1, decoder_1_out2, decoder_1_out3, decoder_1_out4, decoder_1_out5,
       decoder_1_out6, decoder_1_out7;
  wire [15:0] register_1_q, register_2_q, register_3_q, register_4_q, register_5_q, register_6_q,
       register_7_q, register_8_q;

  Decoder #(.select(3), .enable("false")) decoder_1 (
    .out0(decoder_1_out0), .out1(decoder_1_out1), .out2(decoder_1_out2), .out3(decoder_1_out3),
    .out4(decoder_1_out4), .out5(decoder_1_out5), .out6(decoder_1_out6), .out7(decoder_1_out7), .sel(WriteReg));
  and and_1 (and_1_out, decoder_1_out0, RegWriteEnable);
  and and_2 (and_2_out, decoder_1_out1, RegWriteEnable);
  and and_3 (and_3_out, decoder_1_out2, RegWriteEnable);
  and and_4 (and_4_out, decoder_1_out3, RegWriteEnable);
  and and_5 (and_5_out, decoder_1_out4, RegWriteEnable);
  and and_6 (and_6_out, decoder_1_out5, RegWriteEnable);
  and and_7 (and_7_out, decoder_1_out6, RegWriteEnable);
  and and_8 (and_8_out, decoder_1_out7, RegWriteEnable);
  Register #(.width(16), .trigger("falling")) register_1 (
    .D(WriteData), .en(and_1_out), .Q(register_1_q), .clk(clk), .clr(Reset));
  Register #(.width(16), .trigger("falling")) register_2 (
    .D(WriteData), .en(and_2_out), .Q(register_2_q), .clk(clk), .clr(Reset));
  Register #(.width(16), .trigger("falling")) register_3 (
    .D(WriteData), .en(and_3_out), .Q(register_3_q), .clk(clk), .clr(Reset));
  Register #(.width(16), .trigger("falling")) register_4 (
    .D(WriteData), .en(and_4_out), .Q(register_4_q), .clk(clk), .clr(Reset));
  Register #(.width(16), .trigger("falling")) register_5 (
    .D(WriteData), .en(and_5_out), .Q(register_5_q), .clk(clk), .clr(Reset));
  Register #(.width(16), .trigger("falling")) register_6 (
    .D(WriteData), .en(and_6_out), .Q(register_6_q), .clk(clk), .clr(Reset));
  Register #(.width(16), .trigger("falling")) register_7 (
    .D(WriteData), .en(and_7_out), .Q(register_7_q), .clk(clk), .clr(Reset));
  Register #(.width(16), .trigger("falling")) register_8 (
    .D(WriteData), .en(and_8_out), .Q(register_8_q), .clk(clk), .clr(Reset));
  // Probe on register_1_q
  // Probe on register_2_q
  // Probe on register_3_q
  // Probe on register_4_q
  // Probe on register_5_q
  // Probe on register_6_q
  // Probe on register_7_q
  // Probe on register_8_q
  Multiplexer #(.select(3), .width(16), .enable("false")) multiplexer_1 (
    .in0(register_1_q), .in1(register_2_q), .in2(register_3_q), .in3(register_4_q), .in4(register_5_q),
    .in5(register_6_q), .in6(register_7_q), .in7(register_8_q), .out(ReadData1), .sel(ReadReg1));
  Multiplexer #(.select(3), .width(16), .enable("false")) multiplexer_2 (
    .in0(register_1_q), .in1(register_2_q), .in2(register_3_q), .in3(register_4_q), .in4(register_5_q),
    .in5(register_6_q), .in6(register_7_q), .in7(register_8_q), .out(ReadData2), .sel(ReadReg2));

  // Other names for the same wires on the sheet: data[15:0] = WriteData; R1[2:0] = ReadReg1; R2[2:0] = ReadReg2;
  //   WE = RegWriteEnable
endmodule

module InstrDecoder (
  input  [15:0] ROMInput,
  output [3:0] op,
  output [2:0] rs,
  output [2:0] rt,
  output [2:0] rd,
  output [2:0] shamt,
  output [11:0] j,
  output [5:0] imm
);


  assign imm = ROMInput[5:0];
  assign j = ROMInput[11:0];
  assign op = ROMInput[15:12];
  assign rd = ROMInput[5:3];
  assign rs = ROMInput[11:9];
  assign rt = ROMInput[8:6];
  assign shamt = ROMInput[2:0];
endmodule

module Control (
  input  [3:0] op,
  output [2:0] ALUOp,
  output Load,
  output [1:0] NewPCSelect,
  output ChangePC,
  output TTYOn,
  output ReadKey,
  output [1:0] WSelect,
  output WE,
  output M1,
  output [1:0] DestSelect
);

  wire add, addi, and_1_out, and_2_out, and_3_out, and_4_out, and_5_out, blt, bne, imm_out, j, jal, jr,
       jump_out, lw, \not , or_2_out, or_3_out, or_4_out, or_5_out, rt_out, sll, sra, sub, sw, \xor ;

  and u_not (\not , ~op[3], ~op[2], ~op[1], ~op[0]);  // AND_Gate
  and u_xor (\xor , ~op[3], ~op[2], ~op[1], op[0]);  // AND_Gate
  and and_1 (and_1_out, ~lw, ~ReadKey, ~jal);  // AND_Gate
  or imm (imm_out, addi, lw, sw);
  and u_add (add, ~op[3], ~op[2], op[1], op[0]);  // AND_Gate
  and u_addi (addi, ~op[3], ~op[2], op[1], ~op[0]);  // AND_Gate
  or or_1 (ChangePC, blt, bne, jal, j, jr);
  or rt (rt_out, \xor , add, sub, blt, bne);
  and and_2 (and_2_out, ~rt_out, ~imm_out);  // AND_Gate
  and u_sub (sub, ~op[3], op[2], ~op[1], ~op[0]);  // AND_Gate
  and and_3 (and_3_out, ~sub, ~\not , ~\xor , ~sll, ~sra);  // AND_Gate
  or or_2 (or_2_out, rt_out, and_2_out);
  and u_sra (sra, ~op[3], op[2], ~op[1], op[0]);  // AND_Gate
  Priority_Encoder #(.disabled(0)) priority_encoder_1 (
    .in0(and_3_out), .in1(sub), .in2(\not ), .in3(\xor ), .in4(sll), .in5(sra), .out(ALUOp));  // open: in6, in7, en_in, gs, en_out
  Priority_Encoder #(.select(2), .disabled(0)) priority_encoder_2 (
    .in0(and_1_out), .in1(lw), .in2(ReadKey), .in3(jal), .out(WSelect));  // open: gs, en_out, en_in
  Priority_Encoder #(.select(1)) priority_encoder_3 (
    .in0(or_2_out), .in1(imm_out), .out(M1));  // open: gs, en_out, en_in
  and u_lw (lw, ~op[3], op[2], op[1], op[0]);  // AND_Gate
  and u_sll (sll, ~op[3], op[2], op[1], ~op[0]);  // AND_Gate
  and u_sw (sw, op[3], ~op[2], ~op[1], ~op[0]);  // AND_Gate
  and u_j (j, op[3], ~op[2], ~op[1], op[0]);  // AND_Gate
  or or_3 (or_3_out, addi, lw);
  and u_jr (jr, op[3], ~op[2], op[1], op[0]);  // AND_Gate
  and u_jal (jal, op[3], ~op[2], op[1], ~op[0]);  // AND_Gate
  and and_4 (and_4_out, ~sw, ~lw);  // AND_Gate
  or jump (jump_out, jal, j);
  or or_4 (or_4_out, sw, j, jr, bne, blt);
  and and_5 (and_5_out, ~or_3_out, ~jal);  // AND_Gate
  and u_bne (bne, op[3], op[2], ~op[1], ~op[0]);  // AND_Gate
  Priority_Encoder #(.select(1)) priority_encoder_4 (.in0(sw), .in1(or_5_out), .out(Load));  // open: gs, en_out, en_in
  or or_5 (or_5_out, and_4_out, lw);
  not not_2 (WE, or_4_out);
  and u_blt (blt, op[3], op[2], ~op[1], op[0]);  // AND_Gate
  Priority_Encoder #(.select(2)) priority_encoder_5 (
    .in0(and_5_out), .in1(or_3_out), .in2(jal), .out(DestSelect));  // open: in3, gs, en_out, en_in
  and \input  (ReadKey, op[3], op[2], op[1], ~op[0]);  // AND_Gate
  and \output  (TTYOn, op[3], op[2], op[1], op[0]);
  Priority_Encoder #(.select(2), .disabled(0)) priority_encoder_6 (
    .in0(jump_out), .in1(bne), .in2(blt), .in3(jr), .out(NewPCSelect));  // open: gs, en_out, en_in

  // Other names for the same wires on the sheet: input = ReadKey; output = TTYOn
endmodule
